// Logisim project Lab21copy.circ as structural Verilog: 1 circuit, main circuit main
module main (
  input  X,
  input  Y,
  output out_3
);

  wire AND_2_out, AND_out, not_1_out, not_2_out;

  not not_1 (not_1_out, X);
  not not_2 (not_2_out, Y);
  and AND (AND_out, not_1_out, Y);
  and AND_2 (AND_2_out, X, not_2_out);
  or OR (out_3, AND_out, AND_2_out);

  // Notes on the sheet:
  //   XOR Circuit Built Using Logisim
endmodule
