// Logisim project Lab22.circ as structural Verilog: 3 circuits, main circuit main
module main (
  input  Toggle,
  input  [7:0] A,
  input  [7:0] B,
  output [7:0] out_4
);

  _8_bit_Adder u_8_bit_adder_1 (.B(B), .Toggle(Toggle), .A(A), .Output(out_4));

  // Notes on the sheet:
  //   0 = Addition
  //   1 = Subtraction
endmodule

// 8B
module _8_bit_Adder (
  input  [7:0] B,
  input  Toggle,
  input  [7:0] A,
  output [7:0] Output
);

  wire n1_bit_adder_1_cout, n1_bit_adder_1_s, n1_bit_adder_2_cout, n1_bit_adder_2_s, n1_bit_adder_3_cout,
       n1_bit_adder_3_s, n1_bit_adder_4_cout, n1_bit_adder_4_s, n1_bit_adder_5_cout, n1_bit_adder_5_s,
       n1_bit_adder_6_cout, n1_bit_adder_6_s, n1_bit_adder_7_cout, n1_bit_adder_7_s, n1_bit_adder_8_s,
       xor_1_out, xor_2_out, xor_3_out, xor_4_out, xor_5_out, xor_6_out, xor_7_out, xor_8_out;

  xor xor_1 (xor_1_out, A[0], Toggle);
  xor xor_2 (xor_2_out, A[1], Toggle);
  xor xor_3 (xor_3_out, A[2], Toggle);
  xor xor_4 (xor_4_out, A[3], Toggle);
  xor xor_5 (xor_5_out, A[4], Toggle);
  xor xor_6 (xor_6_out, A[5], Toggle);
  xor xor_7 (xor_7_out, A[6], Toggle);
  xor xor_8 (xor_8_out, A[7], Toggle);
  _1_bit_Adder u_1_bit_adder_1 (.Cin(1'b0), .A(xor_1_out), .B(B[0]), .Cout(n1_bit_adder_1_cout), .S(n1_bit_adder_1_s));
  _1_bit_Adder u_1_bit_adder_2 (
    .Cin(n1_bit_adder_1_cout), .A(xor_2_out), .B(B[1]), .Cout(n1_bit_adder_2_cout), .S(n1_bit_adder_2_s));
  _1_bit_Adder u_1_bit_adder_3 (
    .Cin(n1_bit_adder_2_cout), .A(xor_3_out), .B(B[2]), .Cout(n1_bit_adder_3_cout), .S(n1_bit_adder_3_s));
  _1_bit_Adder u_1_bit_adder_4 (
    .Cin(n1_bit_adder_3_cout), .A(xor_4_out), .B(B[3]), .Cout(n1_bit_adder_4_cout), .S(n1_bit_adder_4_s));
  _1_bit_Adder u_1_bit_adder_5 (
    .Cin(n1_bit_adder_4_cout), .A(xor_5_out), .B(B[4]), .Cout(n1_bit_adder_5_cout), .S(n1_bit_adder_5_s));
  _1_bit_Adder u_1_bit_adder_6 (
    .Cin(n1_bit_adder_5_cout), .A(xor_6_out), .B(B[5]), .Cout(n1_bit_adder_6_cout), .S(n1_bit_adder_6_s));
  _1_bit_Adder u_1_bit_adder_7 (
    .Cin(n1_bit_adder_6_cout), .A(xor_7_out), .B(B[6]), .Cout(n1_bit_adder_7_cout), .S(n1_bit_adder_7_s));
  _1_bit_Adder u_1_bit_adder_8 (
    .Cin(n1_bit_adder_7_cout), .A(xor_8_out), .B(B[7]), .S(n1_bit_adder_8_s));  // open: Cout
  xor xor_9 (Output[0], n1_bit_adder_1_s, Toggle);
  xor xor_10 (Output[1], n1_bit_adder_2_s, Toggle);
  xor xor_11 (Output[2], n1_bit_adder_3_s, Toggle);
  xor xor_12 (Output[3], n1_bit_adder_4_s, Toggle);
  xor xor_13 (Output[4], n1_bit_adder_5_s, Toggle);
  xor xor_14 (Output[5], n1_bit_adder_6_s, Toggle);
  xor xor_15 (Output[6], n1_bit_adder_7_s, Toggle);
  xor xor_16 (Output[7], n1_bit_adder_8_s, Toggle);

  // Notes on the sheet:
  //   1=Subtraction
  //   0=Addition
  //   8-bit Adder/Subtractor
endmodule

// 1B
module _1_bit_Adder (
  input  Cin,
  input  A,
  input  B,
  output Cout,
  output S
);

  wire and_1_out, and_2_out, xor_1_out;

  xor xor_1 (xor_1_out, A, B);
  and and_1 (and_1_out, xor_1_out, Cin);
  and and_2 (and_2_out, B, A);
  or or_1 (Cout, and_1_out, and_2_out);
  xor xor_2 (S, Cin, xor_1_out);
endmodule
