// Logisim project Lab23.circ as structural Verilog: 5 circuits, main circuit main
module main (
);

  wire Buy_One_Product___20_Nickels_out, Insert_Dime__2_Nickels_out, Insert_Dollar__20_Nickels_out,
       Insert_Nickle_out, Insert_Quarter__5_Nickels_out, Reset_Button_out;
  wire [7:0] register_1_out_7;

  Button Insert_Nickle (.out(Insert_Nickle_out));
  Button Insert_Dime__2_Nickels (.out(Insert_Dime__2_Nickels_out));
  Button Insert_Quarter__5_Nickels (.out(Insert_Quarter__5_Nickels_out));
  Button Insert_Dollar__20_Nickels (.out(Insert_Dollar__20_Nickels_out));
  Button Buy_One_Product___20_Nickels (.out(Buy_One_Product___20_Nickels_out));
  Button Reset_Button (.out(Reset_Button_out));
  Register register_1 (
    ._5_Cent(Insert_Nickle_out), ._10_Cent(Insert_Dime__2_Nickels_out),
    ._25_Cent(Insert_Quarter__5_Nickels_out), ._1_Dollar(Insert_Dollar__20_Nickels_out),
    .Paying(Buy_One_Product___20_Nickels_out), .out_7(register_1_out_7), .Reset(Reset_Button_out));
  Hex_Digit_Display hex_digit_display_1 (.value(register_1_out_7[7:4]));  // open: dp
  Hex_Digit_Display hex_digit_display_2 (.value(register_1_out_7[3:0]));  // open: dp

  // Notes on the sheet:
  //   Hexadecimal in Terms of Nickles
  //   1 dollar = 20 nickels
  //   100 nickels = 64 in hex
endmodule

// 8B
module _8_bit_Circuit (
  input  [7:0] B,
  input  Toggle,
  input  [7:0] A,
  output [7:0] Output
);

  wire n1_bit_circuit_1_cout, n1_bit_circuit_1_s, n1_bit_circuit_2_cout, n1_bit_circuit_2_s,
       n1_bit_circuit_3_cout, n1_bit_circuit_3_s, n1_bit_circuit_4_cout, n1_bit_circuit_4_s,
       n1_bit_circuit_5_cout, n1_bit_circuit_5_s, n1_bit_circuit_6_cout, n1_bit_circuit_6_s,
       n1_bit_circuit_7_cout, n1_bit_circuit_7_s, n1_bit_circuit_8_s, xor_1_out, xor_2_out, xor_3_out,
       xor_4_out, xor_5_out, xor_6_out, xor_7_out, xor_8_out;

  xor xor_1 (xor_1_out, A[0], Toggle);
  xor xor_2 (xor_2_out, A[1], Toggle);
  xor xor_3 (xor_3_out, A[2], Toggle);
  xor xor_4 (xor_4_out, A[3], Toggle);
  xor xor_5 (xor_5_out, A[4], Toggle);
  xor xor_6 (xor_6_out, A[5], Toggle);
  xor xor_7 (xor_7_out, A[6], Toggle);
  xor xor_8 (xor_8_out, A[7], Toggle);
  _1_bit_Circuit u_1_bit_circuit_1 (
    .Cin(1'b0), .A(xor_1_out), .B(B[0]), .Cout(n1_bit_circuit_1_cout), .S(n1_bit_circuit_1_s));
  _1_bit_Circuit u_1_bit_circuit_2 (
    .Cin(n1_bit_circuit_1_cout), .A(xor_2_out), .B(B[1]), .Cout(n1_bit_circuit_2_cout), .S(n1_bit_circuit_2_s));
  _1_bit_Circuit u_1_bit_circuit_3 (
    .Cin(n1_bit_circuit_2_cout), .A(xor_3_out), .B(B[2]), .Cout(n1_bit_circuit_3_cout), .S(n1_bit_circuit_3_s));
  _1_bit_Circuit u_1_bit_circuit_4 (
    .Cin(n1_bit_circuit_3_cout), .A(xor_4_out), .B(B[3]), .Cout(n1_bit_circuit_4_cout), .S(n1_bit_circuit_4_s));
  _1_bit_Circuit u_1_bit_circuit_5 (
    .Cin(n1_bit_circuit_4_cout), .A(xor_5_out), .B(B[4]), .Cout(n1_bit_circuit_5_cout), .S(n1_bit_circuit_5_s));
  _1_bit_Circuit u_1_bit_circuit_6 (
    .Cin(n1_bit_circuit_5_cout), .A(xor_6_out), .B(B[5]), .Cout(n1_bit_circuit_6_cout), .S(n1_bit_circuit_6_s));
  _1_bit_Circuit u_1_bit_circuit_7 (
    .Cin(n1_bit_circuit_6_cout), .A(xor_7_out), .B(B[6]), .Cout(n1_bit_circuit_7_cout), .S(n1_bit_circuit_7_s));
  _1_bit_Circuit u_1_bit_circuit_8 (
    .Cin(n1_bit_circuit_7_cout), .A(xor_8_out), .B(B[7]), .S(n1_bit_circuit_8_s));  // open: Cout
  xor xor_9 (Output[0], n1_bit_circuit_1_s, Toggle);
  xor xor_10 (Output[1], n1_bit_circuit_2_s, Toggle);
  xor xor_11 (Output[2], n1_bit_circuit_3_s, Toggle);
  xor xor_12 (Output[3], n1_bit_circuit_4_s, Toggle);
  xor xor_13 (Output[4], n1_bit_circuit_5_s, Toggle);
  xor xor_14 (Output[5], n1_bit_circuit_6_s, Toggle);
  xor xor_15 (Output[6], n1_bit_circuit_7_s, Toggle);
  xor xor_16 (Output[7], n1_bit_circuit_8_s, Toggle);

  // Notes on the sheet:
  //   1=Subtraction
  //   0=Addition
  //   8-bit Adder/Subtractor
endmodule

// 1B
module _1_bit_Circuit (
  input  Cin,
  input  A,
  input  B,
  output Cout,
  output S
);

  wire and_1_out, and_2_out, xor_1_out;

  xor xor_1 (xor_1_out, A, B);
  and and_1 (and_1_out, xor_1_out, Cin);
  and and_2 (and_2_out, B, A);
  or or_1 (Cout, and_1_out, and_2_out);
  xor xor_2 (S, Cin, xor_1_out);
endmodule

// R
module Register (
  input  _5_Cent,
  input  _10_Cent,
  input  _25_Cent,
  input  _1_Dollar,
  input  Paying,
  input  Reset,
  output [7:0] out_7
);

  wire comparator_adding_money_1_output, comparator_adding_money_2_output, comparator_adding_money_3_output,
       comparator_adding_money_4_output;
  wire [7:0] n8_bit_circuit_1_output, n8_bit_circuit_2_output, n8_bit_circuit_3_output,
       n8_bit_circuit_4_output, n8_bit_circuit_5_output, n8_bit_circuit_6_output, n8_bit_circuit_7_output,
       n8_bit_circuit_8_output, register_1_q, register_2_q, register_3_q, register_4_q, register_5_q;

  Comparator__Adding_money comparator_adding_money_1 (
    .Added(8'h1), .Money(out_7), .Input(_5_Cent), .\output (comparator_adding_money_1_output));
  Comparator__Adding_money comparator_adding_money_2 (
    .Added(8'h2), .Money(out_7), .Input(_10_Cent), .\output (comparator_adding_money_2_output));
  Comparator__Adding_money comparator_adding_money_3 (
    .Added(8'h5), .Money(out_7), .Input(_25_Cent), .\output (comparator_adding_money_3_output));
  Comparator__Adding_money comparator_adding_money_4 (
    .Added(8'h14), .Money(out_7), .Input(_1_Dollar), .\output (comparator_adding_money_4_output));
  _8_bit_Circuit u_8_bit_circuit_1 (.B(register_1_q), .Toggle(1'b0), .A(8'h1), .Output(n8_bit_circuit_1_output));
  _8_bit_Circuit u_8_bit_circuit_2 (.B(register_2_q), .Toggle(1'b0), .A(8'h2), .Output(n8_bit_circuit_2_output));
  _8_bit_Circuit u_8_bit_circuit_3 (.B(register_3_q), .Toggle(1'b0), .A(8'h5), .Output(n8_bit_circuit_3_output));
  _8_bit_Circuit u_8_bit_circuit_4 (.B(register_4_q), .Toggle(1'b0), .A(8'h14), .Output(n8_bit_circuit_4_output));
  _8_bit_Circuit u_8_bit_circuit_5 (.B(register_5_q), .Toggle(1'b0), .A(8'h14), .Output(n8_bit_circuit_5_output));
  Register_part #(.trigger("falling")) register_1 (
    .D(n8_bit_circuit_1_output), .en(1'b1), .Q(register_1_q), .clk(comparator_adding_money_1_output),
    .clr(Reset));
  Register_part #(.trigger("falling")) register_2 (
    .D(n8_bit_circuit_2_output), .en(1'b1), .Q(register_2_q), .clk(comparator_adding_money_2_output),
    .clr(Reset));
  Register_part #(.trigger("falling")) register_3 (
    .D(n8_bit_circuit_3_output), .en(1'b1), .Q(register_3_q), .clk(comparator_adding_money_3_output),
    .clr(Reset));
  Register_part #(.trigger("falling")) register_4 (
    .D(n8_bit_circuit_4_output), .en(1'b1), .Q(register_4_q), .clk(comparator_adding_money_4_output),
    .clr(Reset));
  Register_part #(.trigger("falling")) register_5 (
    .D(n8_bit_circuit_5_output), .en(1'b1), .Q(register_5_q), .clk(Paying), .clr(Reset));
  _8_bit_Circuit u_8_bit_circuit_6 (
    .B(register_1_q), .Toggle(1'b0), .A(register_2_q), .Output(n8_bit_circuit_6_output));
  _8_bit_Circuit u_8_bit_circuit_7 (
    .B(register_3_q), .Toggle(1'b0), .A(register_4_q), .Output(n8_bit_circuit_7_output));
  _8_bit_Circuit u_8_bit_circuit_8 (
    .B(n8_bit_circuit_6_output), .Toggle(1'b0), .A(n8_bit_circuit_7_output), .Output(n8_bit_circuit_8_output));
  _8_bit_Circuit u_8_bit_circuit_9 (.B(register_5_q), .Toggle(1'b1), .A(n8_bit_circuit_8_output), .Output(out_7));
endmodule

module Comparator__Adding_money (
  input  [7:0] Added,
  input  [7:0] Money,
  input  Input,
  output \output 
);

  wire comparator_1_eq, comparator_1_lt, or_1_out;
  wire [7:0] n8_bit_circuit_1_output;

  _8_bit_Circuit u_8_bit_circuit_1 (.B(Added), .Toggle(1'b0), .A(Money), .Output(n8_bit_circuit_1_output));
  Comparator comparator_1 (
    .a(n8_bit_circuit_1_output), .b(8'h64), .eq(comparator_1_eq), .lt(comparator_1_lt));  // open: gt
  or or_1 (or_1_out, comparator_1_eq, comparator_1_lt);
  and and_1 (\output , or_1_out, Input);
endmodule
