// Logisim project Lab24.circ as structural Verilog: 6 circuits, main circuit main
module main (
);

  wire Buy_A_Cheese_Burger___2_25___45_Nickels_out, Buy_A_Double_Cheese_Burger___3_60___72_Nickels_out,
       Buy_A_Large_Soda___1_95___39_Nickels_out, Buy_French_Fries___1_00___20_Nickels_out,
       Insert_Dime__2_Nickels_out, Insert_Dollar__20_Nickels_out, Insert_Nickle_out,
       Insert_Quarter__5_Nickels_out, register_1_led;
  wire [7:0] register_1_output;

  Button Insert_Nickle (.out(Insert_Nickle_out));
  Button Insert_Dime__2_Nickels (.out(Insert_Dime__2_Nickels_out));
  Button Insert_Quarter__5_Nickels (.out(Insert_Quarter__5_Nickels_out));
  Button Insert_Dollar__20_Nickels (.out(Insert_Dollar__20_Nickels_out));
  Button Buy_French_Fries___1_00___20_Nickels (.out(Buy_French_Fries___1_00___20_Nickels_out));
  Button Buy_A_Large_Soda___1_95___39_Nickels (.out(Buy_A_Large_Soda___1_95___39_Nickels_out));
  Button Buy_A_Cheese_Burger___2_25___45_Nickels (.out(Buy_A_Cheese_Burger___2_25___45_Nickels_out));
  Button Buy_A_Double_Cheese_Burger___3_60___72_Nickels (.out(Buy_A_Double_Cheese_Burger___3_60___72_Nickels_out));
  LED led_1 (.in(register_1_led));
  Register register_1 (
    ._5_Cent(Insert_Nickle_out), ._10_Cent(Insert_Dime__2_Nickels_out),
    ._25_Cent(Insert_Quarter__5_Nickels_out), ._1_Dollar(Insert_Dollar__20_Nickels_out),
    .Pay__1_00(Buy_French_Fries___1_00___20_Nickels_out),
    .Pay__1_95(Buy_A_Large_Soda___1_95___39_Nickels_out),
    .Pay__2_25(Buy_A_Cheese_Burger___2_25___45_Nickels_out),
    .Pay__3_60(Buy_A_Double_Cheese_Burger___3_60___72_Nickels_out), .\output (register_1_output),
    .LED(register_1_led));
  Hex_Digit_Display hex_digit_display_1 (.value(register_1_output[7:4]));  // open: dp
  Hex_Digit_Display hex_digit_display_2 (.value(register_1_output[3:0]));  // open: dp

  // Notes on the sheet:
  //   Turns on when there is $5.00 inserted
  //   or when the user tries to buy something
  //   without having enough money inserted
  //   Hexadecimal in Terms of Nickles
  //   1 dollar = 20 nickels
  //   100 nickels = 64 in hex
endmodule

// 8B
module _8_bit_Circuit (
  input  [7:0] B,
  input  Toggle,
  input  [7:0] A,
  output [7:0] Output
);

  wire n1_bit_circuit_1_cout, n1_bit_circuit_1_s, n1_bit_circuit_2_cout, n1_bit_circuit_2_s,
       n1_bit_circuit_3_cout, n1_bit_circuit_3_s, n1_bit_circuit_4_cout, n1_bit_circuit_4_s,
       n1_bit_circuit_5_cout, n1_bit_circuit_5_s, n1_bit_circuit_6_cout, n1_bit_circuit_6_s,
       n1_bit_circuit_7_cout, n1_bit_circuit_7_s, n1_bit_circuit_8_s, xor_1_out, xor_2_out, xor_3_out,
       xor_4_out, xor_5_out, xor_6_out, xor_7_out, xor_8_out;

  xor xor_1 (xor_1_out, A[0], Toggle);
  xor xor_2 (xor_2_out, A[1], Toggle);
  xor xor_3 (xor_3_out, A[2], Toggle);
  xor xor_4 (xor_4_out, A[3], Toggle);
  xor xor_5 (xor_5_out, A[4], Toggle);
  xor xor_6 (xor_6_out, A[5], Toggle);
  xor xor_7 (xor_7_out, A[6], Toggle);
  xor xor_8 (xor_8_out, A[7], Toggle);
  _1_bit_Circuit u_1_bit_circuit_1 (
    .Cin(1'b0), .A(xor_1_out), .B(B[0]), .Cout(n1_bit_circuit_1_cout), .S(n1_bit_circuit_1_s));
  _1_bit_Circuit u_1_bit_circuit_2 (
    .Cin(n1_bit_circuit_1_cout), .A(xor_2_out), .B(B[1]), .Cout(n1_bit_circuit_2_cout), .S(n1_bit_circuit_2_s));
  _1_bit_Circuit u_1_bit_circuit_3 (
    .Cin(n1_bit_circuit_2_cout), .A(xor_3_out), .B(B[2]), .Cout(n1_bit_circuit_3_cout), .S(n1_bit_circuit_3_s));
  _1_bit_Circuit u_1_bit_circuit_4 (
    .Cin(n1_bit_circuit_3_cout), .A(xor_4_out), .B(B[3]), .Cout(n1_bit_circuit_4_cout), .S(n1_bit_circuit_4_s));
  _1_bit_Circuit u_1_bit_circuit_5 (
    .Cin(n1_bit_circuit_4_cout), .A(xor_5_out), .B(B[4]), .Cout(n1_bit_circuit_5_cout), .S(n1_bit_circuit_5_s));
  _1_bit_Circuit u_1_bit_circuit_6 (
    .Cin(n1_bit_circuit_5_cout), .A(xor_6_out), .B(B[5]), .Cout(n1_bit_circuit_6_cout), .S(n1_bit_circuit_6_s));
  _1_bit_Circuit u_1_bit_circuit_7 (
    .Cin(n1_bit_circuit_6_cout), .A(xor_7_out), .B(B[6]), .Cout(n1_bit_circuit_7_cout), .S(n1_bit_circuit_7_s));
  _1_bit_Circuit u_1_bit_circuit_8 (
    .Cin(n1_bit_circuit_7_cout), .A(xor_8_out), .B(B[7]), .S(n1_bit_circuit_8_s));  // open: Cout
  xor xor_9 (Output[0], n1_bit_circuit_1_s, Toggle);
  xor xor_10 (Output[1], n1_bit_circuit_2_s, Toggle);
  xor xor_11 (Output[2], n1_bit_circuit_3_s, Toggle);
  xor xor_12 (Output[3], n1_bit_circuit_4_s, Toggle);
  xor xor_13 (Output[4], n1_bit_circuit_5_s, Toggle);
  xor xor_14 (Output[5], n1_bit_circuit_6_s, Toggle);
  xor xor_15 (Output[6], n1_bit_circuit_7_s, Toggle);
  xor xor_16 (Output[7], n1_bit_circuit_8_s, Toggle);

  // Notes on the sheet:
  //   1=Subtraction
  //   0=Addition
  //   8-bit Adder/Subtractor
endmodule

// 1B
module _1_bit_Circuit (
  input  Cin,
  input  A,
  input  B,
  output Cout,
  output S
);

  wire and_1_out, and_2_out, xor_1_out;

  xor xor_1 (xor_1_out, A, B);
  and and_1 (and_1_out, xor_1_out, Cin);
  and and_2 (and_2_out, B, A);
  or or_1 (Cout, and_1_out, and_2_out);
  xor xor_2 (S, Cin, xor_1_out);
endmodule

// R
module Register (
  input  _5_Cent,
  input  _10_Cent,
  input  _25_Cent,
  input  _1_Dollar,
  input  Pay__1_00,
  input  Pay__1_95,
  input  Pay__2_25,
  input  Pay__3_60,
  output [7:0] \output ,
  output LED
);

  wire clock_1_out, comparator_1_eq, comparator_2_eq, comparator_adding_money_1_output,
       comparator_adding_money_2_output, comparator_adding_money_3_output, comparator_adding_money_4_output,
       comparator_subtracting_money_1_led, comparator_subtracting_money_1_output,
       comparator_subtracting_money_2_led, comparator_subtracting_money_2_output,
       comparator_subtracting_money_3_led, comparator_subtracting_money_3_output,
       comparator_subtracting_money_4_led, comparator_subtracting_money_4_output, or_1_out, or_2_out,
       or_3_out;
  wire [7:0] n8_bit_circuit_1_output, n8_bit_circuit_2_output, n8_bit_circuit_3_output,
       n8_bit_circuit_4_output, n8_bit_circuit_5_output, n8_bit_circuit_6_output, n8_bit_circuit_7_output,
       n8_bit_circuit_8_output, n8_bit_circuit_9_output, n8_bit_circuit_10_output, n8_bit_circuit_11_output,
       n8_bit_circuit_12_output, n8_bit_circuit_13_output, n8_bit_circuit_14_output,
       n8_bit_circuit_15_output, register_1_q, register_2_q, register_3_q, register_4_q, register_5_q,
       register_6_q, register_7_q, register_8_q, register_9_q;

  Comparator__Adding_money comparator_adding_money_1 (
    .Added(8'h1), .Input(\output ), .Input_2(_5_Cent), .\output (comparator_adding_money_1_output));
  Comparator__Adding_money comparator_adding_money_2 (
    .Added(8'h2), .Input(\output ), .Input_2(_10_Cent), .\output (comparator_adding_money_2_output));
  Comparator__Adding_money comparator_adding_money_3 (
    .Added(8'h5), .Input(\output ), .Input_2(_25_Cent), .\output (comparator_adding_money_3_output));
  Comparator__Adding_money comparator_adding_money_4 (
    .Added(8'h14), .Input(\output ), .Input_2(_1_Dollar), .\output (comparator_adding_money_4_output));
  Comparator__Subtracting_money comparator_subtracting_money_1 (
    .Subtracted(8'h14), .Money(\output ), .Input(Pay__1_00),
    .\output (comparator_subtracting_money_1_output), .LED(comparator_subtracting_money_1_led));
  Comparator__Subtracting_money comparator_subtracting_money_2 (
    .Subtracted(8'h27), .Money(\output ), .Input(Pay__1_95),
    .\output (comparator_subtracting_money_2_output), .LED(comparator_subtracting_money_2_led));
  Comparator__Subtracting_money comparator_subtracting_money_3 (
    .Subtracted(8'h2d), .Money(\output ), .Input(Pay__2_25),
    .\output (comparator_subtracting_money_3_output), .LED(comparator_subtracting_money_3_led));
  Comparator__Subtracting_money comparator_subtracting_money_4 (
    .Subtracted(8'h48), .Money(\output ), .Input(Pay__3_60),
    .\output (comparator_subtracting_money_4_output), .LED(comparator_subtracting_money_4_led));
  or or_1 (or_1_out, Pay__3_60, Pay__2_25, Pay__1_95, Pay__1_00, _1_Dollar, _25_Cent, _10_Cent, _5_Cent);
  _8_bit_Circuit u_8_bit_circuit_1 (.B(register_1_q), .Toggle(1'b0), .A(8'h1), .Output(n8_bit_circuit_1_output));
  _8_bit_Circuit u_8_bit_circuit_2 (.B(register_2_q), .Toggle(1'b0), .A(8'h2), .Output(n8_bit_circuit_2_output));
  _8_bit_Circuit u_8_bit_circuit_3 (.B(register_3_q), .Toggle(1'b0), .A(8'h5), .Output(n8_bit_circuit_3_output));
  _8_bit_Circuit u_8_bit_circuit_4 (.B(register_4_q), .Toggle(1'b0), .A(8'h14), .Output(n8_bit_circuit_4_output));
  _8_bit_Circuit u_8_bit_circuit_5 (.B(register_5_q), .Toggle(1'b0), .A(8'h14), .Output(n8_bit_circuit_5_output));
  _8_bit_Circuit u_8_bit_circuit_6 (.B(register_6_q), .Toggle(1'b0), .A(8'h27), .Output(n8_bit_circuit_6_output));
  _8_bit_Circuit u_8_bit_circuit_7 (.B(register_7_q), .Toggle(1'b0), .A(8'h2d), .Output(n8_bit_circuit_7_output));
  _8_bit_Circuit u_8_bit_circuit_8 (.B(register_8_q), .Toggle(1'b0), .A(8'h48), .Output(n8_bit_circuit_8_output));
  Register_part #(.trigger("falling")) register_1 (
    .D(n8_bit_circuit_1_output), .en(1'b1), .Q(register_1_q), .clk(comparator_adding_money_1_output),
    .clr(comparator_1_eq));
  Register_part #(.trigger("falling")) register_2 (
    .D(n8_bit_circuit_2_output), .en(1'b1), .Q(register_2_q), .clk(comparator_adding_money_2_output),
    .clr(comparator_1_eq));
  Register_part #(.trigger("falling")) register_3 (
    .D(n8_bit_circuit_3_output), .en(1'b1), .Q(register_3_q), .clk(comparator_adding_money_3_output),
    .clr(comparator_1_eq));
  Register_part #(.trigger("falling")) register_4 (
    .D(n8_bit_circuit_4_output), .en(1'b1), .Q(register_4_q), .clk(comparator_adding_money_4_output),
    .clr(comparator_1_eq));
  Register_part #(.trigger("falling")) register_5 (
    .D(n8_bit_circuit_5_output), .en(1'b1), .Q(register_5_q), .clk(comparator_subtracting_money_1_output),
    .clr(comparator_1_eq));
  Register_part #(.trigger("falling")) register_6 (
    .D(n8_bit_circuit_6_output), .en(1'b1), .Q(register_6_q), .clk(comparator_subtracting_money_2_output),
    .clr(comparator_1_eq));
  Register_part #(.trigger("falling")) register_7 (
    .D(n8_bit_circuit_7_output), .en(1'b1), .Q(register_7_q), .clk(comparator_subtracting_money_3_output),
    .clr(comparator_1_eq));
  Register_part #(.trigger("falling")) register_8 (
    .D(n8_bit_circuit_8_output), .en(1'b1), .Q(register_8_q), .clk(comparator_subtracting_money_4_output),
    .clr(comparator_1_eq));
  _8_bit_Circuit u_8_bit_circuit_9 (
    .B(register_1_q), .Toggle(1'b0), .A(register_2_q), .Output(n8_bit_circuit_9_output));
  _8_bit_Circuit u_8_bit_circuit_10 (
    .B(register_3_q), .Toggle(1'b0), .A(register_4_q), .Output(n8_bit_circuit_10_output));
  _8_bit_Circuit u_8_bit_circuit_11 (.B(register_9_q), .Toggle(1'b0), .A(8'h1), .Output(n8_bit_circuit_11_output));
  or or_2 (or_2_out, comparator_1_eq, or_1_out);
  _8_bit_Circuit u_8_bit_circuit_12 (
    .B(n8_bit_circuit_9_output), .Toggle(1'b0), .A(n8_bit_circuit_10_output),
    .Output(n8_bit_circuit_12_output));
  Register_part #(.trigger("falling")) register_9 (
    .D(n8_bit_circuit_11_output), .en(1'b1), .Q(register_9_q), .clk(clock_1_out), .clr(or_2_out));
  Clock clock_1 (.out(clock_1_out));
  Comparator comparator_1 (.a(register_9_q), .b(8'h5), .eq(comparator_1_eq));  // open: gt, lt
  _8_bit_Circuit u_8_bit_circuit_13 (
    .B(register_5_q), .Toggle(1'b1), .A(n8_bit_circuit_12_output), .Output(n8_bit_circuit_13_output));
  _8_bit_Circuit u_8_bit_circuit_14 (
    .B(register_6_q), .Toggle(1'b1), .A(n8_bit_circuit_13_output), .Output(n8_bit_circuit_14_output));
  _8_bit_Circuit u_8_bit_circuit_15 (
    .B(register_7_q), .Toggle(1'b1), .A(n8_bit_circuit_14_output), .Output(n8_bit_circuit_15_output));
  _8_bit_Circuit u_8_bit_circuit_16 (.B(register_8_q), .Toggle(1'b1), .A(n8_bit_circuit_15_output), .Output(\output ));
  Comparator comparator_2 (.a(\output ), .b(8'h64), .eq(comparator_2_eq));  // open: gt, lt
  or or_3 (or_3_out, comparator_subtracting_money_1_led, comparator_subtracting_money_2_led, comparator_subtracting_money_3_led, comparator_subtracting_money_4_led);
  or or_4 (LED, comparator_2_eq, or_3_out);
endmodule

// CA
module Comparator__Adding_money (
  input  [7:0] Added,
  input  [7:0] Input,
  input  Input_2,
  output \output 
);

  wire comparator_1_eq, comparator_1_lt, or_1_out;
  wire [7:0] n8_bit_circuit_1_output;

  _8_bit_Circuit u_8_bit_circuit_1 (.B(Added), .Toggle(1'b0), .A(Input), .Output(n8_bit_circuit_1_output));
  Comparator comparator_1 (
    .a(n8_bit_circuit_1_output), .b(8'h64), .eq(comparator_1_eq), .lt(comparator_1_lt));  // open: gt
  or or_1 (or_1_out, comparator_1_eq, comparator_1_lt);
  and and_1 (\output , or_1_out, Input_2);
endmodule

// CS
module Comparator__Subtracting_money (
  input  [7:0] Subtracted,
  input  [7:0] Money,
  input  Input,
  output \output ,
  output LED
);

  wire comparator_1_eq, comparator_1_gt, comparator_1_lt, or_1_out;
  wire [7:0] n8_bit_circuit_1_output, n8_bit_circuit_2_output;

  _8_bit_Circuit u_8_bit_circuit_1 (.B(8'h14), .Toggle(1'b0), .A(Money), .Output(n8_bit_circuit_1_output));
  Comparator comparator_1 (
    .a(n8_bit_circuit_2_output), .b(8'h14), .gt(comparator_1_gt), .eq(comparator_1_eq), .lt(comparator_1_lt));
  or or_1 (or_1_out, comparator_1_gt, comparator_1_eq);
  and and_1 (LED, comparator_1_lt, Input);
  and and_2 (\output , or_1_out, Input);
  _8_bit_Circuit u_8_bit_circuit_2 (
    .B(Subtracted), .Toggle(1'b1), .A(n8_bit_circuit_1_output), .Output(n8_bit_circuit_2_output));
endmodule
