// Logisim project circuitexamples.circ as structural Verilog: 2 circuits, main circuit main
module main (
);

  wire button_1_out, button_2_out, clock_1_out, clock_2_out, d_ff_1_q, d_ff_1_qn;
  wire [3:0] counter_1_q;
  wire [7:0] and_1_out, Mystery_c;

  Clock clock_1 (.out(clock_1_out));
  Button button_1 (.out(button_1_out));
  Button button_2 (.out(button_2_out));
  Clock clock_2 (.out(clock_2_out));
  assign and_1_out = 8'hf & 8'hac;  // AND_Gate and_1, 8 bits wide
  D_Flip_Flop d_ff_1 (
    .clk(clock_1_out), .D(d_ff_1_qn), .Q(d_ff_1_q), .Qn(d_ff_1_qn), .en(1'b1), .reset(button_1_out));  // open: preset
  Counter #(.width(4), .max('hf)) counter_1 (
    .Q(counter_1_q), .clk(clock_2_out), .clr(button_2_out));  // open: load, D, count, carry
  Mystery Mystery (.A(8'h10), .B(8'h1a), .C(Mystery_c));
  Hex_Digit_Display hex_digit_display_1 (.value(and_1_out[7:4]));  // open: dp
  LED led_1 (.in(d_ff_1_q));
  Hex_Digit_Display hex_digit_display_2 (.value(counter_1_q));  // open: dp
  Hex_Digit_Display hex_digit_display_3 (.value(Mystery_c[7:4]));  // open: dp
  Hex_Digit_Display hex_digit_display_4 (.value(and_1_out[3:0]));  // open: dp
  Hex_Digit_Display hex_digit_display_5 (.value(Mystery_c[3:0]));  // open: dp

  // Notes on the sheet:
  //   Circuit #1
  //   Circuit #3
  //   Circuit #4: Subcircuit Example
  //   Circuit #2: Make sure ticks are enabled in Simulate menu.
endmodule

module Mystery (
  input  [7:0] A,
  input  [7:0] B,
  output [7:0] C
);

  Adder adder_1 (.a(A), .b(B), .out(C), .cin(1'b0));  // open: cout
endmodule
